// Logisim project rcd.circ as structural Verilog: 1 circuit, main circuit main
module main (
  input  [7:0] in_1,
  input  in_2
);

  wire button_1_out, clock_1_out, not_1_out;
  wire [7:0] counter_1_q, main_1_out_5, main_2_out_5, main_3_out_5, undriven, undriven_2, undriven_3;
  wire [9:0] rom_1_data;
  wire [29:10] rom_1_data_2;

  not not_1 (not_1_out, in_2);
  Button button_1 (.out(button_1_out));
  Clock clock_1 (.out(clock_1_out));
  Counter counter_1 (
    .load(in_2), .D(in_1), .count(not_1_out), .Q(counter_1_q), .clk(clock_1_out), .clr(button_1_out));  // open: carry
  ROM #(.dataWidth(30)) rom_1 (.addr(counter_1_q), .data({rom_1_data_2, rom_1_data}));  // open: sel
  RAM_main main_1 (
    .out_5(main_1_out_5), .in_1(rom_1_data_2[29:20]), .in_2(clock_1_out), .in_3(undriven), .in_4(button_1_out));
  RAM_main main_2 (
    .out_5(main_2_out_5), .in_1(rom_1_data_2[19:10]), .in_2(clock_1_out), .in_3(undriven_2),
    .in_4(button_1_out));
  RAM_main main_3 (.out_5(main_3_out_5), .in_1(rom_1_data), .in_2(clock_1_out), .in_3(undriven_3), .in_4(button_1_out));
endmodule
